# Fritzing sketch apsc160_all (saved by Fritzing 0.9.3b)
circuit board: 8.46667cm x 5.64444cm
breadboards: 2

parts:
  U1 = 7-SEGMENT-4DIGIT [package=7-segment-4digit]
  U2 = 7-SEGMENT-4DIGIT [package=7-segment-4digit]
  R1 = Resistor [tolerance=±5% resistance=220 package=THT]
  R4 = Resistor [tolerance=±5% resistance=220 package=THT]
  R5 = Resistor [tolerance=±5% resistance=220 package=THT]
  R6 = Resistor [tolerance=±5% resistance=220 package=THT]
  R7 = Resistor [tolerance=±5% resistance=220 package=THT]
  R8 = Resistor [tolerance=±5% resistance=220 package=THT]
  U3 = 74HC595 [package="DIP16 [THT]"]
  U4 = 74HC595 [package="DIP16 [THT]"]
  R9 = Resistor [tolerance=±5% resistance=220 package=THT]
  R3 = Resistor [tolerance=±5% resistance=220 package=THT]
  Part2 = Arduino Uno (Rev3)
  SW2 = DIP SWITCH [package=dipswitch-02]
  T2 = TMP36 Temperature Sensor [package="TO92 [THT]"]
  R19 = Rotary Potentiometer (Large) [maximum_resistance=100kΩ package=THT]
  R20 = PHOTOCELL [package=photocell]
  S5 = Pushbutton [package="[THT]"]
  S6 = Pushbutton [package="[THT]"]
  S7 = Pushbutton [package="[THT]"]
  S8 = Pushbutton [package="[THT]"]
  R21 = Resistor [tolerance=±10% resistance=10k package=THT]
  R22 = Resistor [tolerance=±10% resistance=10k package=THT]
  R23 = Resistor [tolerance=±10% resistance=10k package=THT]
  R24 = Resistor [tolerance=±10% resistance=10k package=THT]
  R25 = Resistor [tolerance=±10% resistance=10k package=THT]
  R26 = Resistor [tolerance=±10% resistance=10k package=THT]
  R27 = Resistor [tolerance=±10% resistance=10k package=THT]
  R28 = Resistor [tolerance=±10% resistance=220 package=THT]
  R29 = Resistor [tolerance=±10% resistance=220 package=THT]
  R30 = Resistor [tolerance=±10% resistance=220 package=THT]
  R31 = Resistor [tolerance=±10% resistance=220 package=THT]
  R32 = Resistor [tolerance=±10% resistance=220 package=THT]
  R33 = Resistor [tolerance=±10% resistance=220 package=THT]
  R34 = Resistor [tolerance=±10% resistance=220 package=THT]
  LED12 = LED - 5mm [color="Green (555nm)" package="5 mm [THT]"]
  LED13 = LED - 5mm [color="Yellow (585nm)" package="5 mm [THT]"]
  LED14 = LED - 5mm [color="Red (633nm)" package="5 mm [THT]"]
  LED15 = LED - 5mm [color="Blue (470nm)" package="5 mm [THT]"]
  LED16 = LED - 5mm [color="Green (555nm)" package="5 mm [THT]"]
  LED17 = LED - 5mm [color="Yellow (585nm)" package="5 mm [THT]"]
  LED18 = LED - 5mm [color="Red (633nm)" package="5 mm [THT]"]
  U5 = POT [package=pot_alpha_rv16af-20]

nets:
  N1: U1.1, U3.Q4
  N2: U1.2, U3.Q5
  N3: U1.3, U2.3, R6.Pin_1
  N4: U1.5, U2.5, R5.Pin_1
  N5: U1.6, U3.Q6
  N6: U1.7, U2.7, R1.Pin_1
  N7: U1.8, U3.Q7
  N8: U1.11, U2.11, R4.Pin_0
  N9: U1.13, U2.13, R7.Pin_0
  N10: U1.14, U2.14, R3.Pin_0
  N11: U1.15, U2.15, R9.Pin_0
  N12: U1.16, U2.16, R8.Pin_0
  N13: U2.1, U3.Q0
  N14: U2.2, U3.Q1
  N15: U2.6, U3.Q2
  N16: U2.8, U3.Q3
  N17: R1.Pin_0, U4.Q7
  N18: R4.Pin_1, U4.Q5
  N19: R5.Pin_0, U4.Q4
  N20: R6.Pin_0, U4.Q3
  N21: R7.Pin_1, U4.Q2
  N22: R8.Pin_1, U4.Q1
  GND: U3.GND, U3.OE, U4.GND, Part2.GND, T2.GND, R19.leg1, R21.Pin_1, R22.Pin_1, R23.Pin_0, R24.Pin_1, R25.Pin_0, R26.Pin_0, R27.Pin_1, R28.Pin_1, R29.Pin_1, R30.Pin_1, R31.Pin_1, R32.Pin_1, R34.Pin_1, U5.A
  N23: U3.Q7', U4.DS
  VCC: U3.MR, U3.VCC, U4.MR, U4.VCC, Part2.5V, SW2.1, SW2.2, T2.+Vs, R19.leg2, R20.P$2, S5.Pin_3, S5.Pin_4, S6.Pin_3, S6.Pin_4, S7.Pin_3, S7.Pin_4, S8.Pin_3, S8.Pin_4, U5.E
  N24: U3.SH_CP, U4.SH_CP, Part2.D0/RX
  N25: U3.ST_CP, U4.ST_CP, Part2.D1/TX
  N26: U3.DS, Part2.D2
  N27: U4.Q6, R9.Pin_1
  N28: U4.Q0, R3.Pin_1
  N29: Part2.A0, U5.S
  N30: Part2.A1, R19.wiper
  N31: Part2.A2, R20.P$1, R25.Pin_1
  N32: Part2.A3, T2.Vout
  N33: Part2.A4/SDA, SW2.4, R23.Pin_1
  N34: Part2.A5/SCL, SW2.3, R26.Pin_1
  N35: Part2.D8, S7.Pin_1, S7.Pin_2, R21.Pin_0
  N36: Part2.D9_PWM, S6.Pin_1, S6.Pin_2, R27.Pin_0
  N37: Part2.D10_PWM/SS, S5.Pin_1, S5.Pin_2, R22.Pin_0
  N38: Part2.D11_PWM/MOSI, LED16.anode
  N39: Part2.D12/MISO, LED17.anode
  N40: Part2.D13/SCK, LED18.anode
  N41: Part2.D3_PWM, LED12.anode
  N42: Part2.D4, LED13.anode
  N43: Part2.D5_PWM, LED14.anode
  N44: Part2.D6_PWM, LED15.anode
  N45: Part2.D7, S8.Pin_1, S8.Pin_2, R24.Pin_0
  N46: R28.Pin_0, LED13.cathode
  N47: R29.Pin_0, LED12.cathode
  N48: R30.Pin_0, LED14.cathode
  N49: R31.Pin_0, LED15.cathode
  N50: R32.Pin_0, LED17.cathode
  N51: R33.Pin_0, LED16.cathode
  N52: R34.Pin_0, LED18.cathode
