# Fritzing sketch apsc160_display (saved by Fritzing 0.9.3b)
circuit board: 8.46667cm x 5.64444cm
breadboards: 1

parts:
  U1 = 7-SEGMENT-4DIGIT [package=7-segment-4digit]
  U2 = 7-SEGMENT-4DIGIT [package=7-segment-4digit]
  R1 = Resistor [tolerance=±5% resistance=220 package=THT]
  R4 = Resistor [tolerance=±5% resistance=220 package=THT]
  R5 = Resistor [tolerance=±5% resistance=220 package=THT]
  R6 = Resistor [tolerance=±5% resistance=220 package=THT]
  R7 = Resistor [tolerance=±5% resistance=220 package=THT]
  R8 = Resistor [tolerance=±5% resistance=220 package=THT]
  U3 = 74HC595 [package="DIP16 [THT]"]
  U4 = 74HC595 [package="DIP16 [THT]"]
  R9 = Resistor [tolerance=±5% resistance=220 package=THT]
  R3 = Resistor [tolerance=±5% resistance=220 package=THT]
  UNO = Arduino Uno (Rev3) - ICSP

nets (from the breadboard view):
  N1: U1.1, U3.Q4
  N2: U1.2, U3.Q5
  N3: U1.3, U2.3, R6.Pin_1
  N4: U1.5, U2.5
  N5: U1.7, U2.7
  N6: U1.11, U2.11, R4.Pin_0
  N7: U1.13, U2.13, R7.Pin_0
  N8: U1.14, U2.14, R3.Pin_0
  N9: U2.1, U3.Q0
  N10: U2.2, U3.Q1
  N11: U2.6, U3.Q2
  N12: U2.8, U3.Q3
  N13: U2.16, R8.Pin_0
  N14: R1.Pin_0, U4.Q7
  N15: R4.Pin_1, U4.Q5
  N16: R5.Pin_0, U4.Q4
  N17: R6.Pin_0, U4.Q3
  N18: R7.Pin_1, U4.Q2
  N19: R8.Pin_1, U4.Q1
  GND: U3.GND, UNO.GND
  N20: U3.Q7', U4.DS
  VCC: U3.MR, U3.VCC, U4.MR, UNO.5V
  N21: U3.SH_CP, U4.SH_CP, UNO.D3_PWM
  N22: U3.ST_CP, U4.ST_CP, UNO.D4
  N23: U3.DS, UNO.D2
  N24: U4.Q6, R9.Pin_1
  N25: U4.Q0, R3.Pin_1
