# Fritzing sketch apsc160_rotateLEDs (saved by Fritzing 0.9.3b)
breadboards: 1

parts:
  Part1 = Arduino Uno (Rev3)
  LED4 = LED - 5mm [color="Green (555nm)" package="5 mm [THT]"]
  S4 = Pushbutton [package="[THT]"]
  R3 = Resistor [tolerance=±10% resistance=220 package=THT]
  LED6 = LED - 5mm [color="Yellow (585nm)" package="5 mm [THT]"]
  LED7 = LED - 5mm [color="Red (633nm)" package="5 mm [THT]"]
  R4 = Resistor [tolerance=±10% resistance=220 package=THT]
  R5 = Resistor [tolerance=±10% resistance=220 package=THT]
  R9 = Resistor [tolerance=±10% resistance=10k package=THT]
  R16 = Resistor [tolerance=±10% resistance=220 package=THT]
  LED9 = LED - 5mm [color="Red (633nm)" package="5 mm [THT]"]
  LED10 = LED - 5mm [color="Yellow (585nm)" package="5 mm [THT]"]
  R17 = Resistor [tolerance=±10% resistance=220 package=THT]
  LED11 = LED - 5mm [color="Green (555nm)" package="5 mm [THT]"]
  R18 = Resistor [tolerance=±10% resistance=220 package=THT]

nets:
  N1: Part1.D8, LED9.anode
  N2: Part1.D2, S4.Pin_1, S4.Pin_2, R9.Pin_0
  N3: Part1.D3_PWM, LED4.anode
  N4: Part1.D4, LED6.anode
  N5: Part1.D5_PWM, LED7.anode
  N6: Part1.D6_PWM, LED11.anode
  N7: Part1.D7, LED10.anode
  N8: Part1.5V, S4.Pin_3, S4.Pin_4
  N9: Part1.GND, R3.Pin_1, R4.Pin_1, R5.Pin_1, R9.Pin_1, R16.Pin_1, R17.Pin_1
  N10: LED4.cathode, R3.Pin_0
  N11: LED6.cathode, R4.Pin_0
  N12: LED7.cathode, R5.Pin_0
  N13: R16.Pin_0, LED9.cathode
  N14: LED10.cathode, R17.Pin_0
  N15: LED11.cathode, R18.Pin_0
