# Fritzing sketch apsc160_sensors (saved by Fritzing 0.9.3b)
breadboards: 1

parts:
  Part1 = Arduino Uno (Rev3)
  SW1 = DIP SWITCH [package=dipswitch-02]
  T1 = TMP36 Temperature Sensor [package="TO92 [THT]"]
  U1 = POT [package=pot_alpha_rv16af-20]
  R1 = Rotary Potentiometer (Large) [maximum_resistance=100kΩ package=THT]
  R2 = PHOTOCELL [package=photocell]
  S1 = Pushbutton [package="[THT]"]
  S2 = Pushbutton [package="[THT]"]
  LED4 = LED - 5mm [color="Green (555nm)" package="5 mm [THT]"]
  S3 = Pushbutton [package="[THT]"]
  S4 = Pushbutton [package="[THT]"]
  R3 = Resistor [tolerance=±10% resistance=220 package=THT]
  LED6 = LED - 5mm [color="Yellow (585nm)" package="5 mm [THT]"]
  LED7 = LED - 5mm [color="Red (633nm)" package="5 mm [THT]"]
  LED8 = LED - 5mm [color="Blue (470nm)" package="5 mm [THT]"]
  R4 = Resistor [tolerance=±10% resistance=220 package=THT]
  R5 = Resistor [tolerance=±10% resistance=220 package=THT]
  R6 = Resistor [tolerance=±10% resistance=220 package=THT]
  R9 = Resistor [tolerance=±10% resistance=10k package=THT]
  R10 = Resistor [tolerance=±10% resistance=10k package=THT]
  R11 = Resistor [tolerance=±10% resistance=10k package=THT]
  R12 = Resistor [tolerance=±10% resistance=10k package=THT]
  R13 = Resistor [tolerance=±10% resistance=10k package=THT]
  R14 = Resistor [tolerance=±10% resistance=10k package=THT]
  R15 = Resistor [tolerance=±10% resistance=10k package=THT]
  R16 = Resistor [tolerance=±10% resistance=220 package=THT]
  LED9 = LED - 5mm [color="Red (633nm)" package="5 mm [THT]"]
  LED10 = LED - 5mm [color="Yellow (585nm)" package="5 mm [THT]"]
  R17 = Resistor [tolerance=±10% resistance=220 package=THT]
  LED11 = LED - 5mm [color="Green (555nm)" package="5 mm [THT]"]
  R18 = Resistor [tolerance=±10% resistance=220 package=THT]

nets:
  N1: Part1.A0, T1.Vout
  N2: Part1.A1, R2.P$1, R15.Pin_1
  N3: Part1.A2, R1.wiper
  N4: Part1.A3, U1.S
  N5: Part1.A4/SDA, SW1.4, R14.Pin_1
  N6: Part1.A5/SCL, SW1.3, R13.Pin_1
  N7: Part1.D8, S2.Pin_1, S2.Pin_2, R10.Pin_0
  N8: Part1.D9_PWM, S1.Pin_1, S1.Pin_2, R12.Pin_0
  N9: Part1.D10_PWM/SS, LED11.anode
  N10: Part1.D11_PWM/MOSI, LED10.anode
  N11: Part1.D12/MISO, LED9.anode
  GND: Part1.GND, T1.GND, U1.A, R1.leg1, R3.Pin_1, R4.Pin_1, R5.Pin_1, R6.Pin_1, R9.Pin_1, R10.Pin_1, R11.Pin_1, R12.Pin_1, R13.Pin_0, R14.Pin_0, R15.Pin_0, R16.Pin_1, R17.Pin_1
  N12: Part1.D2, LED4.anode
  N13: Part1.D3_PWM, LED6.anode
  N14: Part1.D4, LED7.anode
  N15: Part1.D5_PWM, LED8.anode
  N16: Part1.D6_PWM, S4.Pin_1, S4.Pin_2, R9.Pin_0
  N17: Part1.D7, S3.Pin_1, S3.Pin_2, R11.Pin_0
  N18: Part1.5V, SW1.1, SW1.2, T1.+Vs, U1.E, R1.leg2, R2.P$2, S1.Pin_3, S1.Pin_4, S2.Pin_3, S2.Pin_4, S3.Pin_3, S3.Pin_4, S4.Pin_3, S4.Pin_4
  N19: LED4.cathode, R3.Pin_0
  N20: LED6.cathode, R4.Pin_0
  N21: LED7.cathode, R5.Pin_0
  N22: LED8.cathode, R6.Pin_0
  N23: R16.Pin_0, LED9.cathode
  N24: LED10.cathode, R17.Pin_0
  N25: LED11.cathode, R18.Pin_0
