# Fritzing sketch apsc160_sim1 (saved by Fritzing 0.9.3b)
breadboards: 1

parts:
  Part1 = Arduino Uno (Rev3)
  SW1 = DIP SWITCH [package=dipswitch-02]
  LED4 = LED - 5mm [color="Green (555nm)" package="5 mm [THT]"]
  R3 = Resistor [tolerance=±10% resistance=220 package=THT]
  LED6 = LED - 5mm [color="Yellow (585nm)" package="5 mm [THT]"]
  LED7 = LED - 5mm [color="Red (633nm)" package="5 mm [THT]"]
  R4 = Resistor [tolerance=±10% resistance=220 package=THT]
  R5 = Resistor [tolerance=±10% resistance=220 package=THT]
  R13 = Resistor [tolerance=±10% resistance=10k package=THT]
  R14 = Resistor [tolerance=±10% resistance=10k package=THT]

nets:
  N1: Part1.D2, SW1.4, R14.Pin_1
  N2: Part1.D3_PWM, SW1.3, R13.Pin_1
  N3: Part1.D4, LED4.anode
  N4: Part1.D5_PWM, LED6.anode
  N5: Part1.D6_PWM, LED7.anode
  N6: Part1.5V, SW1.1, SW1.2
  N7: Part1.GND, R3.Pin_1, R4.Pin_1, R5.Pin_1, R13.Pin_0, R14.Pin_0
  N8: LED4.cathode, R3.Pin_0
  N9: LED6.cathode, R4.Pin_0
  N10: LED7.cathode, R5.Pin_0
