# Fritzing sketch apsc160_sim3 (saved by Fritzing 0.9.3b)
breadboards: 1

parts:
  Part1 = Arduino Uno (Rev3)
  R1 = Rotary Potentiometer (Large) [maximum_resistance=100kΩ package=THT]
  LED4 = LED - 5mm [color="Green (555nm)" package="5 mm [THT]"]
  R3 = Resistor [tolerance=±10% resistance=220 package=THT]
  LED6 = LED - 5mm [color="Yellow (585nm)" package="5 mm [THT]"]
  LED7 = LED - 5mm [color="Red (633nm)" package="5 mm [THT]"]
  R4 = Resistor [tolerance=±10% resistance=220 package=THT]
  R5 = Resistor [tolerance=±10% resistance=220 package=THT]
  R6 = Resistor [tolerance=±10% resistance=220 package=THT]
  R18 = Resistor [tolerance=±10% resistance=220 package=THT]
  LED8 = LED - 5mm [color="Blue (470nm)" package="5 mm [THT]"]
  LED9 = LED - 5mm [color="Orange (620nm)" package="5 mm [THT]"]

nets:
  N1: Part1.A2, R1.wiper
  N2: Part1.D10_PWM/SS, LED7.anode
  N3: Part1.D2, LED8.anode
  N4: Part1.D3_PWM, LED4.anode
  N5: Part1.D4, LED6.anode
  N6: Part1.D5_PWM, LED9.anode
  N7: Part1.5V, R1.leg2
  N8: Part1.GND, R1.leg1, R3.Pin_1, R4.Pin_1, R5.Pin_1, R6.Pin_1, R18.Pin_1
  N9: LED4.cathode, R4.Pin_0
  N10: R3.Pin_0, LED8.cathode
  N11: LED6.cathode, R5.Pin_0
  N12: LED7.cathode, R18.Pin_0
  N13: R6.Pin_0, LED9.cathode
