# Fritzing sketch potentiometer (saved by Fritzing 0.9.3b)

parts:
  Resistance1 = Multimeter
  VCC1 = Battery block 9V
  U1 = POT [package=pot_alpha_rv16af-20]

nets:
  N1: Resistance1.Positive, U1.S
  N2: Resistance1.Com, VCC1.-, U1.E
  N3: VCC1.+, U1.A

custom parts:
  Multimeter: A Standard Multimeter in Current mode Thanks to http://www.wpclipart.com for the original artwork.
